// Logisim project logisim.circ as structural Verilog: 1 circuit, main circuit main
module main (
  input  E2,
  input  E1,
  input  E0,
  output A,
  output B,
  output C,
  output E,
  output D
);

  wire and_1_out, and_2_out, and_3_out, and_4_out, not_1_out, not_2_out;

  not not_1 (not_1_out, E2);
  not not_2 (not_2_out, E1);
  not not_3 (A, E0);
  and and_1 (and_1_out, not_2_out, A);
  and and_2 (and_2_out, E0, E1);
  and and_3 (and_3_out, E0, E1);
  and and_4 (and_4_out, not_1_out, not_2_out);
  or or_1 (B, and_1_out, and_2_out);
  or or_2 (C, E2, and_3_out);
  or or_3 (E, and_4_out, E0);

  assign D = A;
endmodule
